// Logisim project mimo_v04b_Control_Unit_Demo.circ as structural Verilog: 1 circuit, main circuit main
module main (
  input  [7:0] in_1,
  input  Flags,
  input  in_3,
  input  opcode,
  input  [6:0] in_5,
  output [7:0] out_6,
  output [7:0] out_7
);

  wire CLK, multiplexer_2_out, Ncmd, or_1_out, reset;
  wire [1:0] addrsel, cond;
  wire [3:0] aluop;
  wire [7:0] multiplexer_1_out, multiplexer_3_out;
  wire [15:0] DROM;
  wire [31:4] CROM;

  nor nor_1 (Ncmd, in_1[0], in_1[1], in_1[2], in_1[3], in_1[5], in_1[6], in_1[7], in_1[4]);
  // Probe on in_1
  // Probe on CROM[21:20]
  LED led_1 (.in(CROM[22]));
  // Probe on in_1
  // Probe on in_1
  // Probe on in_1
  // Probe on in_1
  // Probe on cond
  LED led_2 (.in(CROM[19]));
  ROM #(.dataWidth(32)) rom_1 (.addr(in_1), .data({CROM[31:19], cond, CROM[16:9], addrsel, CROM[6:4], aluop}));
  ROM #(.dataWidth(16)) rom_2 (.addr(in_1), .data(DROM));
  // Probe on in_5
  // Probe on CROM[16:15]
  LED led_3 (.in(CROM[14]));
  or or_1 (or_1_out, in_3, opcode);
  // Probe on {CROM[31:19], cond, CROM[16:9], addrsel, CROM[6:4], aluop}
  LED led_4 (.in(CROM[13]));
  LED led_5 (.in(CROM[12]));
  // Probe on cond
  // Probe on CROM[10:9]
  LED led_6 (.in(CROM[11]));
  // Probe on addrsel
  LED led_7 (.in(CROM[6]));
  Clock clock_1 (.out(CLK));
  // Probe on DROM[7:0]
  Multiplexer #(.width(8)) multiplexer_1 (
    .in0(DROM[7:0]), .in1(DROM[15:8]), .out(multiplexer_1_out), .sel(multiplexer_2_out));
  // Probe on DROM[15:8]
  Multiplexer #(.select(2)) multiplexer_2 (
    .in0(in_3), .in1(or_1_out), .in2(opcode), .in3(Flags), .out(multiplexer_2_out), .sel(cond));
  Multiplexer #(.width(8)) multiplexer_3 (.in0({8{1'b0}}), .in1({1'b0, in_5}), .out(multiplexer_3_out), .sel(CROM[19]));
  // Probe on DROM
  // Probe on CROM[5:4]
  Adder adder_1 (.a(multiplexer_1_out), .b(multiplexer_3_out), .out(out_7));  // open: cin, cout
  // Probe on aluop
  Button u_Reset (.out(reset));
  // Probe on out_7
  // Probe on out_7

  assign out_6 = in_1;

  // Other names for the same wires on the sheet: opcode_t[6:0] = in_5; c = Flags;
  //   CROM (some bits) = {cond, addrsel, aluop}; op2sel[1:0] = CROM[5:4]; datawrite = CROM[6];
  //   pcsel[1:0] = CROM[10:9]; pcload = CROM[11]; dwrite = CROM[12]; irload = CROM[13]; imload = CROM[14];
  //   regsrc[1:0] = CROM[16:15]; indexsel = CROM[19]; datasel[1:0] = CROM[21:20]; swrite = CROM[22];
  //   MicroPC[7:0] = in_1; n = opcode; z = in_3

  // Notes on the sheet:
  //   Mikro PC
  //   Based on: http://minnie.tuhs.org/Programs/UcodeCPU/index.html
  //   v05: Migration to EVO, Debug, Counters, ImmReg Units
  //   Control ROM
  //   Address of third uinstruction is "opcode+2"
  //   contents of rom_1 (hex, n*v repeats v):
  //   2000 80800 11000 39*0 4000 22*0 1000 0 4000 62*0 21 1000c0 800 a00
  //   contents of rom_2 (hex, n*v repeats v):
  //   101 202 40*0 8282 22*0 8484 0 8383 62*0 8485 8484
  //   Microcode Control Unit
  //   Decision ROM
  //   Micro Instruction
  //   Next uPC
  //   Quick tips:
  //   2a [42]:addrsel=pc  imload=1   # JNEZ Rs,immed
  //   84 [132]:   pcincr: pcload=1  pcsel=pc, goto fetch
  //   85 [133]:   jump:  pcload=1  pcsel=immed, goto fetch
  //   1: pcload=1  pcsel=pc, opcode_jump # PC=PC+1, jump to 2+OPC
  //   41 [65]:addrsel=pc  dwrite=1  regsrc=databus  # Load immediate Rd, immed
  //   43 [67]:addrsel=pc  imload=1    # Store Rd into address from immed
  //   82 [130]: aluop=sub  op2sel=const0, if z then pcincr else jump 
  //   Use ctrl+t to manually toggle global clock signal
  //   Use Simulate->Ticks Enabled for automatic clock signal
  //   2:aluop=add  op2sel=treg  dwrite=1  regsrc=aluout, goto fetch  # ALU operations on Rd,Rs,Rt
endmodule
